# Fritzing sketch ir-lamp (saved by Fritzing 0.9.1b)
circuit board: 5.80989cm x 4.56122cm
breadboards: 1

parts:
  PWRSwitch = PowerSwitch Tail II
  JP1 = Header 2 [package=jst-2-pth-ns]
  JP2 = Header 2 [package=jst-2-pth-ns]
  Pro_Trinket_5v = Pro Trinket 5V
  IR-> = female pin header, 3 pins [form="♀ (female)"]
  Switch = female pin header, 2 pins [form="♀ (female)"]

nets (from the pcb view):
  N1: PWRSwitch.+in, Pro_Trinket_5v.D11
  N2: PWRSwitch.-in, JP1.1, Pro_Trinket_5v.GND, IR->.pin2
  N3: JP1.2, JP2.1
  N4: JP2.2, Switch.pin2
  N5: Pro_Trinket_5v.VBAT, Switch.pin1
  N6: Pro_Trinket_5v.+5V, IR->.pin1
  N7: Pro_Trinket_5v.D12, IR->.pin3

notes:
  SJR
  5v
  GND
  Data
  March 2015

custom parts:
  Pro Trinket 5V: The Pro Trinket 5V is like an Arduino Pro Mini with more pins and USB included. Built with the common core Arduino chip, the ATmega328p, it has 18 GPIO, 2 extra analog inputs, 28K of flash, and 2K of RAM. It has onboard USB bootloading support with Optiboot support, so you can either program your Pro Trinket over USB or with a FTDI cable. The Pro Trinket is programmable using the Arduino IDE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
